# Fritzing sketch specs_design (saved by Fritzing 0.8.7b)
circuit board: 8.46667cm x 5.64444cm

parts:
  Part1 = Arduino Nano (Rev3.0)
  VCC1 = Battery block 9V  # not connected
  Part2 = SRF05 Ultrasonic Rangefinder
  Part3 = YL-44 Buzzer

nets:
  GND: Part1.GND, Part2.GND
  N1: Part1.D8, Part3.pin_2
  N2: Part1.D11/MOSI, Part2.Echo
  N3: Part1.D12/MISO, Part2.Trig
  5V: Part1.5V, Part2.VCC

custom parts:
  YL-44 Buzzer: Buzzer

// code stored in the sketch: Darkness.ino
void setup() {

  Serial.begin(9600);

  pinMode(13,OUTPUT);

}

void loop() {

  float sensorValue = analogRead(A0);

  // Reads the analog input ranging from 0 to 1023
  
  Serial.println(sensorValue);

  if(sensorValue<=400)

  {

    digitalWrite(13,HIGH);

  }

  else

  digitalWrite(13,LOW);

}
