# Fritzing sketch white_cane_design (saved by Fritzing 0.8.7b)
breadboards: 1

parts:
  Part1 = SRF05 Ultrasonic Rangefinder
  Part2 = Arduino Nano (Rev3.0)
  J1 = Buzzer

nets:
  VCC: Part1.VCC, Part2.5V
  N1: Part1.Trig, Part2.D9
  N2: Part1.Echo, Part2.D10
  GND: Part1.GND, Part2.GND, J1.pin1
  N3: Part2.D11/MOSI, J1.pin2

custom parts:
  Buzzer: Fixed frequency buzzer
